# Fritzing sketch schematics (saved by Fritzing 1.0.4)
breadboards: 1

parts:
  Composant1 = LSM303 Breakout Board - Tilt-Compensated Compass
  Composant2 = Arduino Uno (Rev3)  # not connected
  Composant3 = Adafruit NeoPixel Shield [part_number="Adafruit #1430"]
  J1 = Piezo Speaker
  U1 = LCD-16X2 [package=lcd-16x2_noholes]
  R1 = Rotary Potentiometer (Small) [maximum_resistance=10kΩ knob_status=50% power=0.5W package=THT]

nets:
  N1: Composant1.SCL_M, Composant3.SCL
  N2: Composant1.SDA_M, Composant3.SDA
  VCC: Composant1.VCC, Composant3.3.3V
  GND: Composant1.GND, Composant3.GND, J1.pin1, U1.VSS, U1.R_W, R1.leg1
  N3: Composant3.ARDUINO_5V, U1.VDD, R1.leg2
  N4: Composant3.D2, U1.DB7
  N5: Composant3.D3, U1.DB6
  N6: Composant3.D4, U1.DB5
  N7: Composant3.D5, U1.DB4
  N8: Composant3.D7, J1.pin2
  N9: Composant3.D12, U1.E
  N10: Composant3.D13, U1.RS
  N11: U1.VO, R1.wiper

custom parts:
  Adafruit NeoPixel Shield: Put on your sunglasses before putting this shield onto your 'duino - 40 eye-blistering RGB LEDs adorn the NeoPixel shield for a blast of configurable color. Arranged in a 5x8 matrix, each pixel is individually addressable. Only one pin (Digital #6) is required to control all the LEDs. You can cut a trace and use nearly any other pin if you need some customization. To make it easy to start, the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
